# Fritzing sketch Wiring (saved by Fritzing 0.9.3b)
# 18650 Li-ion Battery: CC-BY Dr Kristofer Chan, King's College London/Remote-research.org
breadboards: 1

parts:
  U1 = ESP32S-HiLetgo [part_number=ESP32S-HiLetgo]
  Part1 = 16-Channel 12-bit PWM Servo Driver - I2C [part_number=815]
  J1 = Basic Servo
  LCD2004-I2C1 = LCD2004-I2C
  BAT1 = 18650 Li-ion Battery [package=battery-18650]
  BAT2 = 18650 Li-ion Battery [package=battery-18650]
  BAT3 = 18650 Li-ion Battery [package=battery-18650]
  BAT4 = 18650 Li-ion Battery [package=battery-18650]
  BAT5 = 18650 Li-ion Battery [package=battery-18650]
  BAT6 = 18650 Li-ion Battery [package=battery-18650]
  BAT7 = 18650 Li-ion Battery [package=battery-18650]
  BAT8 = 18650 Li-ion Battery [package=battery-18650]
  Mod1 = 2S-BMS
  Part2 = Voltage Sensor 25V
  GSM_SIM_GPSR_SMS_SIM900_SIM1 = SIM800L [package=THT]
  C1 = Electrolytic Capacitor [capacitance=100µF package="200 mil [THT, electrolytic]"]
  J2 = Basic Servo
  J3 = Basic Servo
  J4 = Basic Servo
  J5 = Basic Servo
  J7 = Basic Servo
  U2 = LM2596 step down module
  U3 = LM2596 step down module
  U5 = LM2596 step down module
  J8 = Basic Servo
  U6 = LM2596 step down module
  HLK-PM1 = HLK-PM01

nets:
  N1: U1.GPIO34, Part2.S
  GND: U1.GND, Part1.GND, J1.gnd, LCD2004-I2C1.GND, Mod1.pin3#2, Part2.GND, Part2.-, GSM_SIM_GPSR_SMS_SIM900_SIM1.GND#1, J2.gnd, J3.gnd, J4.gnd, J5.gnd, J7.gnd, U2.IN-, U2.OUT-, U3.IN-, U3.OUT-, U5.IN-, U5.OUT-, J8.gnd, U6.IN-, U6.OUT-, HLK-PM1.-Vo
  VCC: U1.VIN, LCD2004-I2C1.VCC, Mod1.pin3#3, Part2.VCC, Part2.+, U2.IN+, U2.OUT+, U3.IN+, U5.IN+, U6.OUT+
  N2: U1.GPIO21, Part1.SDA, LCD2004-I2C1.SDA
  N3: U1.GPIO22, Part1.SCL, LCD2004-I2C1.SCL
  N4: Part1.PWM6, J7.pulse
  N5: Part1.PWM5, J5.pulse
  N6: Part1.PWM4, J4.pulse
  N7: Part1.PWM3, J3.pulse
  N8: Part1.PWM2, J2.pulse
  N9: Part1.PWM1, J1.pulse
  N10: Part1.PWM0, J8.pulse
  VCC_2: Part1.5.0V, Part1.VCC, J1.vcc, J2.vcc, J3.vcc, J4.vcc, J5.vcc, J7.vcc, U5.OUT+, J8.vcc
  N11: BAT1.-, BAT2.-, BAT3.-, BAT4.-
  N12: BAT1.+, BAT2.+, BAT3.+, BAT4.+, BAT5.-, BAT6.-, BAT7.-, BAT8.-, Mod1.pin1, Mod1.pin2, Mod1.pin3#4
  N13: BAT5.+, BAT6.+, BAT7.+, BAT8.+
  N14: GSM_SIM_GPSR_SMS_SIM900_SIM1.5V, C1.+, U3.OUT+
  N15: GSM_SIM_GPSR_SMS_SIM900_SIM1.GND#5, C1.-
  N16: U6.IN+, HLK-PM1.+Vo

custom parts:
  ESP32S-HiLetgo: HiLetgo ESP-WROOM-32 ESP32 ESP-32S Development Board 2.4GHz Dual-Mode WiFi + Bluetooth Dual Cores Microcontroller The ESP32 integrated with Antenna switches, RF Balun, power amplifiers, low-noise amplifiers, filters, and management modules, and the entire solution occupies the least area of PCB. 2.4 GHz Wi-Fi plus Bluetooth dual-mode chip, with TSMC Ultra-low power consumption 40nm technology,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
  16-Channel 12-bit PWM Servo Driver - I2C: You want to make a cool robot, maybe a hexapod walker, or maybe just a piece of art with a lot of moving parts. Or maybe you want to drive a lot of LEDs with precise PWM output. Using only two pins, control 16 free-running PWM outputs! You can even chain up 62 breakouts to control up to 992 PWM outputs.
  LCD2004-I2C: A standard character display with 4x20 characters. Comes in many colors with LCM2004 IIC attached.
  18650 Li-ion Battery: 18650 li-ion Battery Standard 18650 battery with interactive connectors Creative Common Attribution 4.0 International (CC-BY 4.0) license. Any use of this part requires attribution of Dr Kristofer Chan, Department of Geography, King's College London. Contact kristofer.chan [at] kcl.ac.uk OR kris [at] remote-research.org for further information.
  2S-BMS: 2S-BMS LIPO battery charger / protection unit. Note pcb does not match the board as it will likely connect with wires, so pcb is 5 pads suitable for .1in header pins.
  LM2596 step down module: LM2596 DC-DC step down power supply module 3 A.
